// Logisim project army_hard_coding_competition.circ as structural Verilog
module _5_input_full_adder (
  input  V,
  input  W,
  input  X,
  input  Y,
  input  Z,
  output Sum,
  output Cout
);

  wire and_1_out, and_2_out, and_3_out, and_4_out, and_5_out;

  and and_1 (and_1_out, V, W);
  and and_2 (and_2_out, W, X);
  and and_3 (and_3_out, X, Y);
  and and_4 (and_4_out, Y, Z);
  and and_5 (and_5_out, Z, V);
  ExactlyOne xor_1 (.out(Sum), .in0(Z), .in1(Y), .in2(X), .in3(W), .in4(V));
  or or_1 (Cout, and_1_out, and_2_out, and_3_out, and_4_out, and_5_out);
endmodule

module bin_multiplie_4bit_input (
  input  A,
  input  B,
  input  C,
  input  D,
  input  E,
  input  F,
  input  G,
  input  H,
  output u,
  output v,
  output w,
  output x,
  output q,
  output r,
  output s,
  output t,
  output m,
  output n,
  output o,
  output p,
  output i,
  output j,
  output k,
  output l
);

  and and_1 (u, E, A);
  and and_2 (v, E, B);
  and and_3 (w, E, C);
  and and_4 (x, E, D);
  and and_5 (q, F, A);
  and and_6 (r, F, B);
  and and_7 (s, F, C);
  and and_8 (t, F, D);
  and and_9 (m, G, A);
  and and_10 (n, G, B);
  and and_11 (o, G, C);
  and and_12 (p, G, D);
  and and_13 (i, H, A);
  and and_14 (j, H, B);
  and and_15 (k, H, C);
  and and_16 (l, H, D);
endmodule

module _4_input_full_adder (
  input  W,
  input  X,
  input  Y,
  input  Z,
  output Sum,
  output Cout
);

  wire and_1_out, and_2_out, and_3_out, and_4_out;

  ExactlyOne xor_1 (.out(Sum), .in0(Y), .in1(X), .in2(W));
  and and_1 (and_1_out, W, X);
  and and_2 (and_2_out, X, Y);
  and and_3 (and_3_out, Y, Z);
  and and_4 (and_4_out, Z, W);
  or or_1 (Cout, and_1_out, and_2_out, and_3_out, and_4_out);
endmodule

module _3_input_full_adder (
  input  W,
  input  X,
  input  Y,
  input  Z
);

  wire and_1_out, and_2_out, and_3_out;

  and and_1 (and_1_out, W, X);
  and and_2 (and_2_out, X, Y);
  and and_3 (and_3_out, Y, Z);
endmodule

module _2_input_full_adder (
  input  A,
  input  B,
  output Sum,
  output Cout
);

  xor xor_1 (Sum, B, A);
  and and_1 (Cout, A, B);
endmodule
